# Fritzing sketch Smart Room Controller (saved by Fritzing 0.9.9b)
breadboards: 1

parts:
  Teensy_3_1 = Teensy 3.1
  Push_Button = Pushbutton [package="[THT]"]
  OLED_I2C1 = OLED 128x64 I2C Monochrome Display
  Ethernet_Port = WIZ820io [part_number=WIZ820io]
  RG_encoder = SprkFn RG Encoder [package="DIP (Dual Inline) [THT]"]
  MPU-6050 = InvenSense MPU6050
  JoyStick = KY-023 Dual Axis Joystick Module [package="Breakout board"]
  C1 = Capacitor [package=cap-pth-small2]
  C2 = Capacitor [package=cap-pth-small2]

nets:
  GND: Teensy_3_1.GND, Push_Button.Pin_3, Push_Button.Pin_4, OLED_I2C1.GND, Ethernet_Port.GND, RG_encoder.GND, RG_encoder.B, MPU-6050.GND, JoyStick.GND, C1.2, C2.1
  N1: Teensy_3_1.D1, C2.2
  N2: Teensy_3_1.D2, RG_encoder.A, C1.1
  N3: Teensy_3_1.D3, RG_encoder.+R
  N4: Teensy_3_1.D4, RG_encoder.+G
  N5: Teensy_3_1.D6, JoyStick.SW
  N6: Teensy_3_1.D7, RG_encoder.SW
  N7: Teensy_3_1.D9, Ethernet_Port.nINT, Ethernet_Port.nRESET
  N8: Teensy_3_1.D11, Ethernet_Port.SCLK
  N9: Teensy_3_1.D12, Ethernet_Port.MISO
  N10: Teensy_3_1.D13, Ethernet_Port.nSS
  N11: Teensy_3_1.A2/D16, JoyStick.VRx
  N12: Teensy_3_1.A3/D17, JoyStick.VRy
  N13: Teensy_3_1.A4/D18, OLED_I2C1.SDA
  N14: Teensy_3_1.A5/D19, MPU-6050.SCL
  N15: Teensy_3_1.A9/D23, Push_Button.Pin_1, Push_Button.Pin_2
  VIN: Teensy_3_1.Vin, OLED_I2C1.VDD, Ethernet_Port.VIN, MPU-6050.VCC, JoyStick.+5V

custom parts:
  Pushbutton: A generic pushbutton.
  SprkFn RG Encoder: SparkFun RG Rotary Encoder
  KY-023 Dual Axis Joystick Module: KY-023 Dual-Axis Joystick Module.
